# Fritzing sketch RPi-Fritzing-Capacitor (saved by Fritzing 0.9.3b)
breadboards: 1

parts:
  IC1 = MCP3008 8-channel 10-bit ADC [part_number=MCP3008]
  Raspberry_Pi_1 = Raspberry Pi 3 [part_number=RPI-3-V1.2]
  C1 = Electrolytic Capacitor [capacitance=47µF package="200 mil [THT, electrolytic]"]
  R1 = Resistor [tolerance=±5% resistance=1k package=THT]

nets:
  N1: IC1.no_name_yet#1, C1.+, R1.Pin_0
  N2: IC1.no_name_yet#10, Raspberry_Pi_1.GIPO24
  N3: IC1.no_name_yet#11, Raspberry_Pi_1.GIPO10
  N4: IC1.no_name_yet#12, Raspberry_Pi_1.GIPO9
  N5: IC1.no_name_yet#13, Raspberry_Pi_1.GIPO11
  N6: IC1.no_name_yet#14, Raspberry_Pi_1.GND, C1.-
  N7: IC1.no_name_yet#15, IC1.no_name_yet#16, Raspberry_Pi_1.3v3
  N8: Raspberry_Pi_1.GIPO26, R1.Pin_1
